// Digital circuit 32-bit-reg.dig as structural Verilog
module _32_bit_reg (
  input  [31:0] D,
  input  en,
  input  CLK,
  input  CLR,
  output [31:0] Q
);

  wire [31:0] multiplexer_1_out;

  Multiplexer #(.Bits(32)) multiplexer_1 (.sel(CLR), .in_0(D), .in_1({32{1'b0}}), .out(multiplexer_1_out));
  Register #(.Bits(32)) register_1 (.D(multiplexer_1_out), .C(CLK), .en(en), .Q(Q));
endmodule
