// Digital circuit ALU.dig as structural Verilog
module ALU (
  input  [31:0] A,
  input  [31:0] B,
  input  [2:0] ALUOP,
  input  [31:0] iw,
  output [31:0] R,
  output N,
  output Z,
  output C,
  output V
);

  wire comparator_2_gt, comparator_3_lt, comparator_6_lt;
  wire [31:0] add_1_s, lsl_out, lsr_out, multiplexer_1_out, sub_1_s, sub_2_s;
  wire [63:0] mul_1_mul;

  Add #(.Bits(32)) add_1 (.a(A), .b(B), .c_i(1'b0), .s(add_1_s));  // open: c_o
  Sub #(.Bits(32)) sub_1 (.a(A), .b(B), .c_i(1'b0), .s(sub_1_s));  // open: c_o
  Mul #(.Bits(32)) mul_1 (.a(A), .b(B), .mul(mul_1_mul));
  BarrelShifter #(.Bits(32)) lsl (.in(B), .shift({1'b0, iw[11:7]}), .out(lsl_out));
  BarrelShifter #(.Bits(32), .direction("right")) lsr (.in(B), .shift({1'b0, iw[11:7]}), .out(lsr_out));
  Comparator #(.Bits(32)) comparator_1 (.a(B), .b(A), .gt(C));  // open: eq, lt
  Sub #(.Bits(32)) sub_2 (.a(A), .b(B), .c_i(1'b0), .s(sub_2_s));  // open: c_o
  Comparator #(.Signed("true"), .Bits(32)) comparator_2 (.a(A), .b({32{1'b0}}), .gt(comparator_2_gt));  // open: eq, lt
  Comparator #(.Signed("true"), .Bits(32)) comparator_3 (.a(B), .b({32{1'b0}}), .lt(comparator_3_lt));  // open: gt, eq
  Multiplexer #(.Selector_Bits(2), .Bits(32)) multiplexer_1 (
    .sel(iw[6:5]), .in_0(lsl_out), .in_1(lsr_out), .in_2({32{1'b0}}), .in_3({32{1'b0}}),
    .out(multiplexer_1_out));
  Comparator #(.Signed("true"), .Bits(32)) comparator_4 (.a(sub_1_s), .b({32{1'b0}}), .lt(N));  // open: gt, eq
  Comparator #(.Signed("true"), .Bits(32)) comparator_5 (.a(sub_1_s), .b({32{1'b0}}), .eq(Z));  // open: gt, lt
  Multiplexer #(.Selector_Bits(3), .Bits(32)) multiplexer_2 (
    .sel(ALUOP), .in_0(add_1_s), .in_1(sub_1_s), .in_2(mul_1_mul[31:0]), .in_3(B), .in_4(multiplexer_1_out),
    .in_5({32{1'b0}}), .in_6({32{1'b0}}), .in_7({32{1'b0}}), .out(R));
  Comparator #(.Signed("true"), .Bits(32)) comparator_6 (
    .a(sub_2_s), .b({32{1'b0}}), .lt(comparator_6_lt));  // open: gt, eq
  and and_1 (V, comparator_6_lt, comparator_2_gt, comparator_3_lt);

  // Other names for the same wires on the sheet: shiftType[1:0] = iw[6:5]
endmodule
