// Digital circuit RegisterFile.dig as structural Verilog
module RegisterFile (
  input  [3:0] ReadReg0,
  input  CLK,
  input  [3:0] ReadReg1,
  input  CLR,
  input  WriteEn,
  input  [31:0] WriteData,
  input  [3:0] WriteReg,
  input  [31:0] PC,
  output [31:0] RD0,
  output [31:0] RD1,
  output [31:0] r0,
  output [31:0] r1,
  output [31:0] r2,
  output [31:0] r3,
  output [31:0] r4,
  output [31:0] r5,
  output [31:0] r6,
  output [31:0] r7,
  output [31:0] r8,
  output [31:0] r9,
  output [31:0] r10,
  output [31:0] r11,
  output [31:0] r12,
  output [31:0] r13,
  output [31:0] r14,
  output [31:0] r15,
  output [31:0] STRreg
);

  wire enablereg_1_r0, enablereg_1_r1, enablereg_1_r2, enablereg_1_r3, enablereg_1_r4, enablereg_1_r5,
       enablereg_1_r6, enablereg_1_r7, enablereg_1_r8, enablereg_1_r9, enablereg_1_r10, enablereg_1_r11,
       enablereg_1_r12, enablereg_1_r13, enablereg_1_r14, enablereg_1_r15, r0_t, r1_t, r2_t, r3_t, r4_t,
       r5_t, r6_t, r7_t, r8_t, r9_t, r10_t, r11_t, r12_t, r13_t, r14_t, r15_t;
  wire [31:0] demultiplexer_1_out_0, demultiplexer_1_out_1, demultiplexer_1_out_2, demultiplexer_1_out_3,
       demultiplexer_1_out_4, demultiplexer_1_out_5, demultiplexer_1_out_6, demultiplexer_1_out_7,
       demultiplexer_1_out_8, demultiplexer_1_out_9, demultiplexer_1_out_10, demultiplexer_1_out_11,
       demultiplexer_1_out_12, demultiplexer_1_out_13, demultiplexer_1_out_14;

  enableReg enablereg_1 (
    .WriteEn(WriteEn), .WriteReg(WriteReg), .r0(enablereg_1_r0), .r1(enablereg_1_r1), .r2(enablereg_1_r2),
    .r3(enablereg_1_r3), .r4(enablereg_1_r4), .r5(enablereg_1_r5), .r6(enablereg_1_r6), .r7(enablereg_1_r7),
    .r8(enablereg_1_r8), .r9(enablereg_1_r9), .r10(enablereg_1_r10), .r11(enablereg_1_r11),
    .r12(enablereg_1_r12), .r13(enablereg_1_r13), .r14(enablereg_1_r14), .r15(enablereg_1_r15));
  or or_1 (r0_t, CLR, enablereg_1_r0);
  or or_2 (r1_t, CLR, enablereg_1_r1);
  or or_3 (r2_t, CLR, enablereg_1_r2);
  or or_4 (r3_t, CLR, enablereg_1_r3);
  or or_5 (r4_t, CLR, enablereg_1_r4);
  or or_6 (r5_t, CLR, enablereg_1_r5);
  or or_7 (r6_t, CLR, enablereg_1_r6);
  or or_8 (r7_t, CLR, enablereg_1_r7);
  or or_9 (r8_t, CLR, enablereg_1_r8);
  or or_10 (r9_t, CLR, enablereg_1_r9);
  or or_11 (r10_t, CLR, enablereg_1_r10);
  or or_12 (r11_t, CLR, enablereg_1_r11);
  or or_13 (r12_t, CLR, enablereg_1_r12);
  or or_14 (r13_t, CLR, enablereg_1_r13);
  or or_15 (r14_t, CLR, enablereg_1_r14);
  or or_16 (r15_t, CLR, enablereg_1_r15);
  Demultiplexer #(.Selector_Bits(4), .Bits(32)) demultiplexer_1 (
    .sel(WriteReg), .in(WriteData), .out_0(demultiplexer_1_out_0), .out_1(demultiplexer_1_out_1),
    .out_2(demultiplexer_1_out_2), .out_3(demultiplexer_1_out_3), .out_4(demultiplexer_1_out_4),
    .out_5(demultiplexer_1_out_5), .out_6(demultiplexer_1_out_6), .out_7(demultiplexer_1_out_7),
    .out_8(demultiplexer_1_out_8), .out_9(demultiplexer_1_out_9), .out_10(demultiplexer_1_out_10),
    .out_11(demultiplexer_1_out_11), .out_12(demultiplexer_1_out_12), .out_13(demultiplexer_1_out_13),
    .out_14(demultiplexer_1_out_14));  // open: out_15
  _32_bit_reg _0 (.D(demultiplexer_1_out_0), .en(r0_t), .CLK(CLK), .CLR(CLR), .Q(r0));
  _32_bit_reg u_r1 (.D(demultiplexer_1_out_1), .en(r1_t), .CLK(CLK), .CLR(CLR), .Q(r1));
  _32_bit_reg u_r2 (.D(demultiplexer_1_out_2), .en(r2_t), .CLK(CLK), .CLR(CLR), .Q(r2));
  _32_bit_reg u_r3 (.D(demultiplexer_1_out_3), .en(r3_t), .CLK(CLK), .CLR(CLR), .Q(r3));
  _32_bit_reg u_r4 (.D(demultiplexer_1_out_4), .en(r4_t), .CLK(CLK), .CLR(CLR), .Q(r4));
  _32_bit_reg u_r5 (.D(demultiplexer_1_out_5), .en(r5_t), .CLK(CLK), .CLR(CLR), .Q(r5));
  _32_bit_reg u_r6 (.D(demultiplexer_1_out_6), .en(r6_t), .CLK(CLK), .CLR(CLR), .Q(r6));
  _32_bit_reg r6_2 (.D(demultiplexer_1_out_7), .en(r7_t), .CLK(CLK), .CLR(CLR), .Q(r7));
  _32_bit_reg u_r8 (.D(demultiplexer_1_out_8), .en(r8_t), .CLK(CLK), .CLR(CLR), .Q(r8));
  _32_bit_reg u_r9 (.D(demultiplexer_1_out_9), .en(r9_t), .CLK(CLK), .CLR(CLR), .Q(r9));
  _32_bit_reg u_r10 (.D(demultiplexer_1_out_10), .en(r10_t), .CLK(CLK), .CLR(CLR), .Q(r10));
  _32_bit_reg u_r11 (.D(demultiplexer_1_out_11), .en(r11_t), .CLK(CLK), .CLR(CLR), .Q(r11));
  _32_bit_reg u_r12 (.D(demultiplexer_1_out_12), .en(r12_t), .CLK(CLK), .CLR(CLR), .Q(r12));
  _32_bit_reg u_r13 (.D(demultiplexer_1_out_13), .en(r13_t), .CLK(CLK), .CLR(CLR), .Q(r13));
  _32_bit_reg u_r14 (.D(demultiplexer_1_out_14), .en(r14_t), .CLK(CLK), .CLR(CLR), .Q(r14));
  Multiplexer #(.Selector_Bits(4), .Bits(32)) multiplexer_1 (
    .sel(WriteReg), .in_0(r0), .in_1(r1), .in_2(r2), .in_3(r3), .in_4(r4), .in_5(r5), .in_6(r6), .in_7(r7),
    .in_8(r8), .in_9(r9), .in_10(r10), .in_11(r11), .in_12(r12), .in_13(r13), .in_14(r14), .in_15(PC),
    .out(STRreg));
  Multiplexer #(.Selector_Bits(4), .Bits(32)) multiplexer_2 (
    .sel(ReadReg0), .in_0(r0), .in_1(r1), .in_2(r2), .in_3(r3), .in_4(r4), .in_5(r5), .in_6(r6), .in_7(r7),
    .in_8(r8), .in_9(r9), .in_10(r10), .in_11(r11), .in_12(r12), .in_13(r13), .in_14(r14), .in_15(PC),
    .out(RD0));
  Multiplexer #(.Selector_Bits(4), .Bits(32)) multiplexer_3 (
    .sel(ReadReg1), .in_0(r0), .in_1(r1), .in_2(r2), .in_3(r3), .in_4(r4), .in_5(r5), .in_6(r6), .in_7(r7),
    .in_8(r8), .in_9(r9), .in_10(r10), .in_11(r11), .in_12(r12), .in_13(r13), .in_14(r14), .in_15(PC),
    .out(RD1));

  assign r15 = PC;
endmodule
