// Digital circuit alternativeClock.dig as structural Verilog
module alternativeClock (
  input  CLK,
  output CLK_C,
  output CLK_B,
  output CLK_X,
  output CLK_D,
  output CLK_F,
  output CLK_Y
);

  wire d_ff_1_q, d_ff_2_nq, d_ff_2_q, d_ff_3_q, d_ff_4_q, d_ff_5_nq, d_ff_6_q, not_1_out, not_2_out,
       not_3_out, not_4_out, not_5_out, not_6_out, xor_1_out;

  not not_1 (not_1_out, d_ff_1_q);
  not not_2 (not_2_out, d_ff_2_q);
  D_FF d_ff_1 (.D(not_1_out), .C(d_ff_2_q), .Q(d_ff_1_q), .nQ(CLK_F));
  LED led_1 (.in(CLK));
  xor xor_1 (xor_1_out, not_2_out, CLK);
  D_FF d_ff_2 (.D(xor_1_out), .C(CLK), .Q(d_ff_2_q), .nQ(d_ff_2_nq));
  not not_3 (not_3_out, d_ff_3_q);
  not not_4 (not_4_out, d_ff_4_q);
  not not_5 (not_5_out, CLK_B);
  D_FF d_ff_3 (.D(not_3_out), .C(xor_1_out), .Q(d_ff_3_q), .nQ(CLK_C));
  D_FF d_ff_4 (.D(not_4_out), .C(not_3_out), .Q(d_ff_4_q), .nQ(CLK_D));
  D_FF d_ff_5 (.D(not_5_out), .C(d_ff_2_nq), .Q(CLK_B), .nQ(d_ff_5_nq));
  not not_6 (not_6_out, d_ff_6_q);
  D_FF d_ff_6 (.D(not_6_out), .C(d_ff_5_nq), .Q(d_ff_6_q), .nQ(CLK_X));
  or or_1 (CLK_Y, CLK_X, CLK_F);
endmodule
