// Digital circuit enableReg.dig as structural Verilog
module enableReg (
  input  WriteEn,
  input  [3:0] WriteReg,
  output r0,
  output r1,
  output r2,
  output r3,
  output r4,
  output r5,
  output r6,
  output r7,
  output r8,
  output r9,
  output r10,
  output r11,
  output r12,
  output r13,
  output r14,
  output r15
);

  wire decoder_1_out_0, decoder_1_out_1, decoder_1_out_2, decoder_1_out_3, decoder_1_out_4, decoder_1_out_5,
       decoder_1_out_6, decoder_1_out_7, decoder_1_out_8, decoder_1_out_9, decoder_1_out_10,
       decoder_1_out_11, decoder_1_out_12, decoder_1_out_13, decoder_1_out_14, decoder_1_out_15;

  Decoder #(.Selector_Bits(4)) decoder_1 (
    .sel(WriteReg), .out_0(decoder_1_out_0), .out_1(decoder_1_out_1), .out_2(decoder_1_out_2),
    .out_3(decoder_1_out_3), .out_4(decoder_1_out_4), .out_5(decoder_1_out_5), .out_6(decoder_1_out_6),
    .out_7(decoder_1_out_7), .out_8(decoder_1_out_8), .out_9(decoder_1_out_9), .out_10(decoder_1_out_10),
    .out_11(decoder_1_out_11), .out_12(decoder_1_out_12), .out_13(decoder_1_out_13),
    .out_14(decoder_1_out_14), .out_15(decoder_1_out_15));
  and and_1 (r0, WriteEn, decoder_1_out_0);
  and and_2 (r2, WriteEn, decoder_1_out_2);
  and and_3 (r4, WriteEn, decoder_1_out_4);
  and and_4 (r6, WriteEn, decoder_1_out_6);
  and and_5 (r8, WriteEn, decoder_1_out_8);
  and and_6 (r10, WriteEn, decoder_1_out_10);
  and and_7 (r12, WriteEn, decoder_1_out_12);
  and and_8 (r14, WriteEn, decoder_1_out_14);
  and and_9 (r1, WriteEn, decoder_1_out_1);
  and and_10 (r3, WriteEn, decoder_1_out_3);
  and and_11 (r5, WriteEn, decoder_1_out_5);
  and and_12 (r7, WriteEn, decoder_1_out_7);
  and and_13 (r9, WriteEn, decoder_1_out_9);
  and and_14 (r11, WriteEn, decoder_1_out_11);
  and and_15 (r13, WriteEn, decoder_1_out_13);
  and and_16 (r15, WriteEn, decoder_1_out_15);
endmodule
