// Digital circuit extender.dig as structural Verilog
module extender (
  input  [31:0] IW,
  input  [1:0] EXT,
  output [31:0] extimm
);

  wire [23:0] demultiplexer_1_out_0, demultiplexer_1_out_1;
  wire [31:0] mul_1_mul, multiplexer_1_out;
  wire [63:32] mul_1_mul_2;

  Demultiplexer #(.Bits(24)) demultiplexer_1 (
    .sel(IW[23]), .in(IW[23:0]), .out_0(demultiplexer_1_out_0), .out_1(demultiplexer_1_out_1));
  Multiplexer #(.Bits(32)) multiplexer_1 (
    .sel(IW[23]), .in_0({{8{1'b0}}, demultiplexer_1_out_0}), .in_1({{8{1'b1}}, demultiplexer_1_out_1}),
    .out(multiplexer_1_out));
  Mul #(.Bits(32)) mul_1 (.a(multiplexer_1_out), .b(32'h4), .mul({mul_1_mul_2, mul_1_mul}));
  Multiplexer #(.Selector_Bits(2), .Bits(32)) multiplexer_2 (
    .sel(EXT), .in_0({{24{1'b0}}, IW[7:0]}), .in_1({{20{1'b0}}, IW[11:0]}), .in_2(mul_1_mul),
    .in_3({32{1'b0}}), .out(extimm));
endmodule
