// Digital circuit inst-mem.dig as structural Verilog
module inst_mem (
  input  [7:0] A,
  input  [3:0] PROGS,
  output [31:0] OUT
);

  wire [31:0] FibRec_2_d, FibRec_d, FindMax_2_d, FindMax_d, max3_2_d, max3_d, merge_2_d, merge_3_d, merge_d,
       merge_sort_11_d, merge_sort_12_d, quad1_d, quad2_d, quad14_d, quad15_d;

  ROM #(.AddrBits(8), .Bits(32)) quad1 (.A(A), .sel(1'b1), .D(quad1_d));
  ROM #(.AddrBits(8), .Bits(32)) quad2 (.A(A), .sel(1'b1), .D(quad2_d));
  ROM #(.AddrBits(8), .Bits(32)) max3 (.A(A), .sel(1'b1), .D(max3_d));
  ROM #(.AddrBits(8), .Bits(32)) max3_2 (.A(A), .sel(1'b1), .D(max3_2_d));
  ROM #(.AddrBits(8), .Bits(32)) FindMax (.A(A), .sel(1'b1), .D(FindMax_d));
  ROM #(.AddrBits(8), .Bits(32)) FindMax_2 (.A(A), .sel(1'b1), .D(FindMax_2_d));
  ROM #(.AddrBits(8), .Bits(32)) FibRec (.A(A), .sel(1'b1), .D(FibRec_d));
  ROM #(.AddrBits(8), .Bits(32)) FibRec_2 (.A(A), .sel(1'b1), .D(FibRec_2_d));
  ROM #(.AddrBits(8), .Bits(32)) merge (.A(A), .sel(1'b1), .D(merge_d));
  ROM #(.AddrBits(8), .Bits(32)) merge_2 (.A(A), .sel(1'b1), .D(merge_2_d));
  ROM #(.AddrBits(8), .Bits(32)) merge_3 (.A(A), .sel(1'b1), .D(merge_3_d));
  ROM #(.AddrBits(8), .Bits(32)) merge_sort_11 (.A(A), .sel(1'b1), .D(merge_sort_11_d));
  ROM #(.AddrBits(8), .Bits(32)) merge_sort_12 (.A(A), .sel(1'b1), .D(merge_sort_12_d));
  ROM #(.AddrBits(8), .Bits(32)) quad14 (.A(A), .sel(1'b1), .D(quad14_d));
  ROM #(.AddrBits(8), .Bits(32)) quad15 (.A(A), .sel(1'b1), .D(quad15_d));
  Multiplexer #(.Selector_Bits(4), .Bits(32)) multiplexer_1 (
    .sel(PROGS), .in_0(quad1_d), .in_1(quad2_d), .in_2(max3_d), .in_3(max3_2_d), .in_4(FindMax_d),
    .in_5(FindMax_2_d), .in_6(FibRec_d), .in_7(FibRec_2_d), .in_8(merge_d), .in_9(merge_2_d),
    .in_10(merge_3_d), .in_11(merge_sort_11_d), .in_12(merge_sort_12_d), .in_13(quad14_d), .in_14(quad15_d),
    .in_15({32{1'b0}}), .out(OUT));

  // Notes on the sheet:
  //   contents of quad1 (hex, n*v repeats v):
  //   e3a00001,e3a01001,e3a02001,e3a03001,eb000000,e2800000,e00c0090,e001019c,e0020290,
  //   e0810002,e0800003,e12fff1e
  //   contents of quad2 (hex, n*v repeats v):
  //   e3a00002,e3a01002,e3a02003,e3a03004,eb000000,e2800000,e00c0090,e001019c,e0020290,
  //   e0810002,e0800003,e12fff1e
  //   contents of max3 (hex, n*v repeats v):
  //   e3a00001,e3a01002,e3a02003,eb000004,e2800000,e1500001,ca000000,e1a00001,e12fff1e,
  //   e24dd008,e58de000,ebfffff8,e1a01002,ebfffff6,e59de000,e28dd008,e12fff1e
  //   contents of max3_2 (hex, n*v repeats v):
  //   e3a0001e,e3a0100a,e3a02014,eb000004,e2800000,e1500001,ca000000,e1a00001,e12fff1e,
  //   e24dd008,e58de000,ebfffff8,e1a01002,ebfffff6,e59de000,e28dd008,e12fff1e
  //   contents of FindMax (hex, n*v repeats v):
  //   e3a0d080,e08dd00d,e08dd00d,e08dd00d,e08dd00d,e08dd00d,e24dd014,e3a00001,e58d0000,
  //   e3a00002,e58d0004,e3a00003,e58d0008,e3a00004,e58d000c,e3a00005,e58d0010,e1a0000d,
  //   e3a01005,e3a02000,e3a03000,eb000000,e2800000,e3a02001,e5903000,e1520001,aa000009,
  //   e1a02102,e0800002,e590c000,e0400002,e1a02122,e15c0003,da000000,e1a0300c,e2822001,
  //   eafffff3,e1a00003,e12fff1e
  //   contents of FindMax_2 (hex, n*v repeats v):
  //   e3a0d080,e08dd00d,e08dd00d,e08dd00d,e08dd00d,e08dd00d,e24dd028,e3a00001,e58d0000,
  //   e3a00063,e58d0004,e3a00001,e58d0008,e3a00002,e58d000c,e3a00003,e58d0010,e3a00004,
  //   e58d0014,e3a00005,e58d0018,e3a00006,e58d001c,e3a00007,e58d0020,e3a00000,e58d0024,
  //   e1a0000d,e3a0100a,e3a02000,e3a03000,eb000000,e2800000,e3a02001,e5903000,e1520001,
  //   aa000008,e1a02102,e0800002,e1a02122,e590c000,e15c0003,da000000,e1a0300c,e2822001,
  //   eafffff4,e1a00003,e12fff1e
  //   contents of FibRec (hex, n*v repeats v):
  //   e3a0000a,e28dd080,e08dd00d,e08dd00d,e08dd00d,e08dd00d,eb000000,e2800000,e24dd010,
  //   e58de000,e3500000,a00000a,e3500001,a000008,e58d0004,e2400001,ebfffff6,e58d0008,e59d0004,
  //   e2400002,ebfffff2,e59d1008,e0800001,e59de000,e28dd010,e12fff1e
  //   contents of FibRec_2 (hex, n*v repeats v):
  //   e3a00013,eb000006,e2800000,e28dd080,e08dd00d,e08dd00d,e08dd00d,e08dd00d,e08dd00d,
  //   e24dd010,e58de000,e3500000,a00000a,e3500001,a000008,e58d0004,e2400001,ebfffff6,e58d0008,
  //   e59d0004,e2400002,ebfffff2,e59d1008,e0800001,e59de000,e28dd010,e12fff1e
  //   contents of merge (hex, n*v repeats v):
  //   e3a0d080,e08dd00d,e08dd00d,e08dd00d,e08dd00d,e08dd00d,e24dd008,e3a00002,e58d0000,
  //   e3a00001,e58d0004,e1a0000d,e24dd008,e3a03002,e58d3000,e3a03001,e58d3004,e1a0300d,
  //   e3a01000,e3a02002,e3a0a000,e3a0b000,eb000000,e2800000,e0814002,e1a040a4,e2845001,
  //   e2844001,e1a06001,e1a08002,e1a09001,e1560002,aa00003a,e15a0004,1a00000b,e1a05105,
  //   e0800005,e590c000,e0400005,e1a05125,e1a06106,e0833006,e583c000,e0433006,e1a06126,
  //   e2855001,ea00002a,e2822001,e152000b,1a00000c,e1a01101,e0800001,e590c000,e0400001,
  //   e1a01121,e1a06106,e0833006,e583c000,e0433006,e1a06126,e2811001,e2422001,ea00001a,
  //   e2422001,e1a01101,e0800001,e5907000,e0400001,e1a01121,e1a05105,e0800005,e590c000,
  //   e0400005,e1a05125,e157000c,aa000006,e1a06106,e0833006,e5837000,e0433006,e1a06126,
  //   e2811001,ea000006,e1a06106,e0833006,e583c000,e0433006,e1a06126,e2855001,eaffffff,
  //   e2866001,eaffffc2,e3a06000,e1560008,ca000009,e1a06106,e0833006,e0800006,e5937000,
  //   e0433006,e5807000,e0400006,e1a06126,e2866001,eafffff3,e12fff1e
  //   contents of merge_2 (hex, n*v repeats v):
  //   e3a0d080,e08dd00d,e08dd00d,e08dd00d,e08dd00d,e08dd00d,e24dd008,e3a00001,e58d0000,
  //   e3a00001,e58d0004,e1a0000d,e24dd008,e3a00000,e58d0008,e58d000c,e1a0300d,e3a01000,
  //   e3a02002,eb000000,e2800000,e0814002,e1a040a4,e2845001,e2844001,e1a06001,e1a08002,
  //   e1a09001,e2422001,e1560002,aa000032,e15a0004,1a000009,e1a05105,e0800005,e1a05125,
  //   e590c000,e1a06106,e0833006,e1a06126,e583c000,e2855001,ea000024,e2822001,e152000b,
  //   1a00000a,e1a01101,e0800001,e1a01121,e590c000,e1a06106,e0833006,e1a06126,e583c000,
  //   e2811001,e2422001,ea000016,e2422001,e1a01101,e0800001,e1a01121,e5907000,e1a05105,
  //   e0800005,e1a05125,e590c000,e157000c,aa000005,e1a06106,e0833006,e1a06126,e5837000,
  //   e2811001,ea000005,e1a06106,e0833006,e1a06126,e583c000,e2855001,eaffffff,e2866001,
  //   eaffffca,e3a06000,e1560008,ca000007,e1a06106,e0833006,e0800006,e5937000,e5807000,
  //   e1a06126,e2866001,eafffff5,e12fff1e
  //   contents of merge_3 (hex, n*v repeats v):
  //   e3a0d080,e08dd00d,e08dd00d,e08dd00d,e08dd00d,e08dd00d,e24dd028,e3a00002,e58d0000,
  //   e3a00004,e58d0004,e3a00008,e58d0008,e3a0000a,e58d000c,e3a0000b,e58d0010,e3a00001,
  //   e58d0014,e3a00003,e58d0018,e3a00007,e58d001c,e3a00009,e58d0020,e3a00009,e58d0024,
  //   e1a0000d,e24dd028,e3a00000,e58d0028,e58d002c,e58d0030,e58d0034,e58d0038,e58d003c,
  //   e58d0040,e58d0044,e58d0048,e58d004c,e1a0300d,e3a01000,e3a0200a,eb000000,e2800000,
  //   e0814002,e1a040a4,e2845001,e2844001,e1a06001,e1a08002,e1a09001,e2422001,e1560002,
  //   aa000032,e15a0004,1a000009,e1a05105,e0800005,e1a05125,e590c000,e1a06106,e0833006,
  //   e1a06126,e583c000,e2855001,ea000024,e2822001,e152000b,1a00000a,e1a01101,e0800001,
  //   e1a01121,e590c000,e1a06106,e0833006,e1a06126,e583c000,e2811001,e2422001,ea000016,
  //   e2422001,e1a01101,e0800001,e1a01121,e5907000,e1a05105,e0800005,e1a05125,e590c000,
  //   e157000c,aa000005,e1a06106,e0833006,e1a06126,e5837000,e2811001,ea000005,e1a06106,
  //   e0833006,e1a06126,e583c000,e2855001,eaffffff,e2866001,eaffffca,e3a06000,e1560008,
  //   ca000007,e1a06106,e0833006,e0800006,e5937000,e5807000,e1a06126,e2866001,eafffff5,
  //   e12fff1e
  //   contents of merge_sort_11 (hex, n*v repeats v):
  //   e3a0d080,e08dd00d,e08dd00d,e08dd00d,e08dd00d,e08dd00d,e24dd004,e3a00001,e58d0000,
  //   e1a0000d,e24dd004,e3a03000,e58d3004,e1a0300d,e3a01000,e3a02001,eb000049,e2800000,
  //   e0814002,e1a040a4,e2845001,e2844001,e1a06001,e1a08002,e1a09001,e2422001,e1560002,
  //   aa000032,e15a0004,1a000009,e1a05105,e0800005,e1a05125,e590c000,e1a06106,e0833006,
  //   e1a06126,e583c000,e2855001,ea000024,e2822001,e152000b,1a00000a,e1a01101,e0800001,
  //   e1a01121,e590c000,e1a06106,e0833006,e1a06126,e583c000,e2811001,e2422001,ea000016,
  //   e2422001,e1a01101,e0800001,e1a01121,e5907000,e1a05105,e0800005,e1a05125,e590c000,
  //   e157000c,aa000005,e1a06106,e0833006,e1a06126,e5837000,e2811001,ea000005,e1a06106,
  //   e0833006,e1a06126,e583c000,e2855001,eaffffff,e2866001,eaffffca,e3a06000,e1560008,
  //   ca000007,e1a06106,e0833006,e0800006,e5937000,e5807000,e1a06126,e2866001,eafffff5,
  //   e12fff1e,e24dd020,e58de000,e1520001,da000011,e0814002,e1a040a4,e58d1004,e58d2008,
  //   e58d400c,e1a02004,ebfffff4,e59d400c,e59d2008,e59d1004,e58d1004,e58d2008,e2844001,
  //   e1a01004,ebffffec,e59d2008,e59d1004,ebffffa0,e59de000,e28dd020,e12fff1e
  //   contents of merge_sort_12 (hex, n*v repeats v):
  //   e3a0d080,e08dd00d,e08dd00d,e08dd00d,e08dd00d,e08dd00d,e24dd008,e3a00002,e58d0000,
  //   e3a00001,e58d0004,e1a0000d,e24dd008,e3a03000,e58d3008,e58d300c,e1a0300d,e3a01000,
  //   e3a02002,eb000049,e2800000,e0814002,e1a040a4,e2845001,e2844001,e1a06001,e1a08002,
  //   e1a09001,e2422001,e1560002,aa000032,e15a0004,1a000009,e1a05105,e0800005,e1a05125,
  //   e590c000,e1a06106,e0833006,e1a06126,e583c000,e2855001,ea000024,e2822001,e152000b,
  //   1a00000a,e1a01101,e0800001,e1a01121,e590c000,e1a06106,e0833006,e1a06126,e583c000,
  //   e2811001,e2422001,ea000016,e2422001,e1a01101,e0800001,e1a01121,e5907000,e1a05105,
  //   e0800005,e1a05125,e590c000,e157000c,aa000005,e1a06106,e0833006,e1a06126,e5837000,
  //   e2811001,ea000005,e1a06106,e0833006,e1a06126,e583c000,e2855001,eaffffff,e2866001,
  //   eaffffca,e3a06000,e1560008,ca000007,e1a06106,e0833006,e0800006,e5937000,e5807000,
  //   e1a06126,e2866001,eafffff5,e12fff1e,e24dd020,e58de000,e1520001,da000011,e0814002,
  //   e1a040a4,e58d1004,e58d2008,e58d400c,e1a02004,ebfffff4,e59d400c,e59d2008,e59d1004,
  //   e58d1004,e58d2008,e2844001,e1a01004,ebffffec,e59d2008,e59d1004,ebffffa0,e59de000,
  //   e28dd020,e12fff1e
  //   contents of quad14 (hex, n*v repeats v):
  //   e3a00001,e3a01001,e3a02001,e3a03001,eb000000,e2800000,e00c0090,e001019c,e0020290,
  //   e0810002,e0800003,e12fff1e
  //   contents of quad15 (hex, n*v repeats v):
  //   e3a00001,e3a01001,e3a02001,e3a03001,eb000000,e2800000,e00c0090,e001019c,e0020290,
  //   e0810002,e0800003,e12fff1e
endmodule
