// Digital circuit iw_decoder_new.dig as structural Verilog
module iw_decoder_new (
  input  [31:0] IW,
  input  CLK,
  input  [3:0] NZCV,
  output RFW,
  output [1:0] EXTop,
  output ALUsrcB,
  output [2:0] ALUOP,
  output [1:0] RR0sel,
  output RR1sel,
  output [1:0] PCsel,
  output [1:0] WRsel,
  output WDsel,
  output MR,
  output MW
);

  wire AL_eq, and_1_out, and_2_out, and_3_out, and_4_out, and_5_out, and_6_out, C, comparator_1_eq,
       comparator_2_eq, comparator_3_eq, comparator_4_eq, condex, EQ_eq, GE_eq, GT_eq, iw_decoder_v2_1_cpsrw,
       LE_eq, LT_eq, N, NE_eq, not_1_out, not_2_out, not_3_out, not_4_out, or_1_out, V, Z;
  wire [1:0] iw_decoder_v2_1_pcsel;

  Register #(.Bits(4)) CPSR (.D(NZCV), .C(CLK), .en(iw_decoder_v2_1_cpsrw), .Q({V, C, Z, N}));
  Comparator #(.Bits(4)) LE (.a(IW[31:28]), .b(4'b1101), .eq(LE_eq));  // open: gt, lt
  iw_decoder_v2 iw_decoder_v2_1 (
    .IW(IW), .RFW(RFW), .EXTop(EXTop), .ALUsrcB(ALUsrcB), .ALUOP(ALUOP), .PCsel(iw_decoder_v2_1_pcsel),
    .RR0sel(RR0sel), .RR1sel(RR1sel), .WRsel(WRsel), .WDsel(WDsel), .MR(MR), .MW(MW),
    .CPSRW(iw_decoder_v2_1_cpsrw));
  Comparator #(.Bits(4)) GE (.a(IW[31:28]), .b(4'b1010), .eq(GE_eq));  // open: gt, lt
  Comparator #(.Bits(4)) GT (.a(IW[31:28]), .b(4'b1100), .eq(GT_eq));  // open: gt, lt
  Comparator #(.Bits(4)) LT (.a(IW[31:28]), .b(4'b1011), .eq(LT_eq));  // open: gt, lt
  Comparator comparator_1 (.a(N), .b(V), .eq(comparator_1_eq));  // open: gt, lt
  Comparator #(.Bits(4)) AL (.a(IW[31:28]), .b(4'b1110), .eq(AL_eq));  // open: gt, lt
  Comparator #(.Bits(4)) EQ (.a(IW[31:28]), .b(4'b0000), .eq(EQ_eq));  // open: gt, lt
  Comparator #(.Bits(4)) NE (.a(IW[31:28]), .b(4'b0001), .eq(NE_eq));  // open: gt, lt
  Comparator comparator_2 (.a(N), .b(V), .eq(comparator_2_eq));  // open: gt, lt
  not not_1 (not_1_out, Z);
  Comparator comparator_3 (.a(N), .b(V), .eq(comparator_3_eq));  // open: gt, lt
  Comparator comparator_4 (.a(N), .b(V), .eq(comparator_4_eq));  // open: gt, lt
  not not_2 (not_2_out, comparator_1_eq);
  and and_1 (and_1_out, Z, EQ_eq);
  not not_3 (not_3_out, Z);
  not not_4 (not_4_out, comparator_4_eq);
  or or_1 (or_1_out, Z, not_2_out);
  and and_2 (and_2_out, not_3_out, NE_eq);
  and and_3 (and_3_out, comparator_2_eq, GE_eq);
  and and_4 (and_4_out, not_1_out, comparator_3_eq, GT_eq);
  and and_5 (and_5_out, not_4_out, LT_eq);
  and and_6 (and_6_out, or_1_out, LE_eq);
  or or_2 (condex, AL_eq, and_1_out, and_2_out, and_3_out, and_4_out, and_5_out, and_6_out, 1'b0);
  Multiplexer #(.Bits(2)) multiplexer_1 (.sel(condex), .in_0(2'b00), .in_1(iw_decoder_v2_1_pcsel), .out(PCsel));
  // Probe on RFW
  // Probe on EXTop
  // Probe on ALUsrcB
  // Probe on ALUOP
  // Probe on RR0sel
  // Probe on RR1sel
  // Probe on WRsel
  // Probe on WDsel
  // Probe on MR
  // Probe on MW
endmodule
