// Digital circuit iw_decoder_v2.dig as structural Verilog
module iw_decoder_v2 (
  input  [31:0] IW,
  output RFW,
  output [1:0] EXTop,
  output ALUsrcB,
  output [2:0] ALUOP,
  output [1:0] RR0sel,
  output RR1sel,
  output [1:0] PCsel,
  output [1:0] WRsel,
  output WDsel,
  output MR,
  output MW,
  output CPSRW
);

  wire Add__i_eq, Add_r_eq, and_1_out, b_eq, bl_eq, bx_eq, Cmp_i_eq, Cmp_r_eq, comparator_1_eq,
       comparator_2_eq, comparator_3_eq, LDR_i_eq, Mov_i_eq, Mov_r_eq, MUL_r_eq, str_eq, Sub_i_eq, Sub_r_eq;
  wire [3:0] priorityencoder_1_num;
  wire [16:16] multiplexer_1_out;

  // Probe on IW[27:20]
  // Probe on IW[27:24]
  // Probe on IW[27:4]
  // Probe on IW[27:22]
  // Probe on IW[7:4]
  // Probe on IW[27:21]
  Comparator #(.Bits(8)) Add_r (.a(IW[27:20]), .b(8'h8), .eq(Add_r_eq));  // open: gt, lt
  Comparator #(.Bits(8)) Mov_i (.a(IW[27:20]), .b(8'h3a), .eq(Mov_i_eq));  // open: gt, lt
  Comparator #(.Bits(4)) b (.a(IW[27:24]), .b(4'b1010), .eq(b_eq));  // open: gt, lt
  Comparator #(.Bits(4)) bl (.a(IW[27:24]), .b(4'b1011), .eq(bl_eq));  // open: gt, lt
  Comparator #(.Bits(24)) bx (.a(IW[27:4]), .b(24'h12fff1), .eq(bx_eq));  // open: gt, lt
  Comparator #(.Bits(6)) MUL_r (.a(IW[27:22]), .b({6{1'b0}}), .eq(MUL_r_eq));  // open: gt, lt
  Comparator #(.Bits(4)) comparator_1 (.a(IW[7:4]), .b(4'b1001), .eq(comparator_1_eq));  // open: gt, lt
  Comparator #(.Bits(8)) Add__i (.a(IW[27:20]), .b(8'h28), .eq(Add__i_eq));  // open: gt, lt
  Comparator #(.Bits(8)) Mov_r (.a(IW[27:20]), .b(8'h1a), .eq(Mov_r_eq));  // open: gt, lt
  Comparator #(.Bits(8)) Sub_i (.a(IW[27:20]), .b(8'h24), .eq(Sub_i_eq));  // open: gt, lt
  Comparator #(.Bits(8)) Sub_r (.a(IW[27:20]), .b(8'h4), .eq(Sub_r_eq));  // open: gt, lt
  Comparator #(.Bits(7)) Cmp_i (.a(IW[27:21]), .b(7'b0011010), .eq(Cmp_i_eq));  // open: gt, lt
  Comparator #(.Bits(7)) Cmp_r (.a(IW[27:21]), .b(7'b0001010), .eq(Cmp_r_eq));  // open: gt, lt
  Comparator #(.Bits(8)) str (.a(IW[27:20]), .b(8'h58), .eq(str_eq));  // open: gt, lt
  Comparator #(.Bits(8)) LDR_i (.a(IW[27:20]), .b(8'h59), .eq(LDR_i_eq));  // open: gt, lt
  and and_1 (and_1_out, MUL_r_eq, comparator_1_eq);
  PriorityEncoder #(.Selector_Bits(4)) priorityencoder_1 (
    .in0(Add_r_eq), .in1(Mov_i_eq), .in2(b_eq), .in3(bl_eq), .in4(bx_eq), .in5(and_1_out), .in6(Add__i_eq),
    .in7(Mov_r_eq), .in8(Sub_i_eq), .in9(Sub_r_eq), .in10(Cmp_i_eq), .in11(Cmp_r_eq), .in12(str_eq),
    .in13(LDR_i_eq), .in14(1'b0), .in15(1'b0), .num(priorityencoder_1_num));  // open: any
  Multiplexer #(.Selector_Bits(4), .Bits(18)) multiplexer_1 (
    .sel(priorityencoder_1_num), .in_0(18'h20000), .in_1(18'h22c00), .in_2(18'ha140), .in_3(18'h2a14c),
    .in_4(18'h200), .in_5(18'h20890), .in_6(18'h22000), .in_7(18'h21000), .in_8(18'h22400), .in_9(18'h20400),
    .in_10(18'h2800), .in_11(18'h800), .in_12(18'h6001), .in_13(18'h26002), .in_14({18{1'b0}}),
    .in_15({18{1'b0}}),
    .out({RFW, multiplexer_1_out[16], EXTop, ALUsrcB, ALUOP, PCsel, RR0sel, RR1sel, WRsel, WDsel, MR, MW}));
  Comparator #(.Bits(4)) comparator_2 (.a(priorityencoder_1_num), .b(4'b1011), .eq(comparator_2_eq));  // open: gt, lt
  Comparator #(.Bits(4)) comparator_3 (.a(priorityencoder_1_num), .b(4'b1010), .eq(comparator_3_eq));  // open: gt, lt
  // Probe on {RFW, multiplexer_1_out[16], EXTop, ALUsrcB, ALUOP, PCsel, RR0sel, RR1sel, WRsel, WDsel, MR, MW}
  or or_1 (CPSRW, comparator_2_eq, comparator_3_eq);
  // Probe on RFW
  // Probe on EXTop
  // Probe on ALUsrcB
  // Probe on ALUOP
  // Probe on PCsel
  // Probe on RR0sel
  // Probe on RR1sel
  // Probe on WRsel
  // Probe on WDsel
  // Probe on MR
  // Probe on MW

  // Other names for the same wires on the sheet: bits_4_7[3:0] = IW[7:4]; bits_4_27[23:0] = IW[27:4];
  //   bits_20_27[7:0] = IW[27:20]; bits_21_27[6:0] = IW[27:21]; bits_22_27[5:0] = IW[27:22];
  //   bits_24_27[3:0] = IW[27:24]
endmodule
