// Digital circuit project06.dig as structural Verilog
module project06 (
  input  CLK,
  input  [3:0] PROG,
  input  CLR,
  output [31:0] R0,
  output DONE
);

  wire a_mul, ALUsrcB, clk_t, i_dp, MR, MW, not_1_out, or_1_out, RFW, RR1sel, WDsel;
  wire [1:0] EXTop, PCsel, RR0sel, WRsel;
  wire [2:0] ALUop;
  wire [3:0] cond, multiplexer_2_out, multiplexer_3_out, multiplexer_5_out, NCZV;
  wire [23:0] b_offset;
  wire [27:24] iw;
  wire [31:0] _32_bit_reg_1_q, add_1_s, add_2_s, alu_1_r, extender_1_extimm, multiplexer_1_out,
       multiplexer_4_out, multiplexer_6_out, multiplexer_7_out, r1, r2, r3, r4, r5, r6, r7, r8, r9, r10, r11,
       r12, r13, r14, r15, ramdualport_1_d, registerfile_1_rd0, registerfile_1_rd1, registerfile_1_strreg;

  not not_1 (not_1_out, DONE);
  or or_1 (or_1_out, not_1_out, CLR);
  and and_1 (clk_t, CLK, or_1_out);
  _32_bit_reg _32_bit_reg_1 (.D(multiplexer_1_out), .en(1'b1), .CLK(clk_t), .CLR(CLR), .Q(_32_bit_reg_1_q));
  // Probe on PCsel
  Multiplexer #(.Selector_Bits(2), .Bits(32)) multiplexer_1 (
    .sel(PCsel), .in_0(add_1_s), .in_1(multiplexer_7_out), .in_2(registerfile_1_rd1), .in_3({32{1'b0}}),
    .out(multiplexer_1_out));
  // Probe on {cond, iw[27:26], i_dp, iw[24], b_offset[23:22], a_mul, b_offset[20:0]}
  inst_mem inst_mem_1 (
    .A(_32_bit_reg_1_q[9:2]), .PROGS(PROG),
    .OUT({cond, iw[27:26], i_dp, iw[24], b_offset[23:22], a_mul, b_offset[20:0]}));
  Add #(.Bits(32)) add_1 (.a(_32_bit_reg_1_q), .b(32'h4), .c_i(1'b0), .s(add_1_s));  // open: c_o
  iw_decoder_new iw_decoder_new_1 (
    .IW({cond, iw[27:26], i_dp, iw[24], b_offset[23:22], a_mul, b_offset[20:0]}), .NZCV(NCZV), .CLK(clk_t),
    .RFW(RFW), .EXTop(EXTop), .ALUsrcB(ALUsrcB), .ALUOP(ALUop), .PCsel(PCsel), .RR0sel(RR0sel),
    .RR1sel(RR1sel), .WRsel(WRsel), .WDsel(WDsel), .MR(MR), .MW(MW));
  Add #(.Bits(32)) add_2 (.a(add_1_s), .b(32'h4), .c_i(1'b0), .s(add_2_s));  // open: c_o
  // Probe on R0
  // Probe on r1
  // Probe on r2
  // Probe on r3
  // Probe on r4
  // Probe on cond
  // Probe on iw[27:26]
  // Probe on i_dp
  // Probe on {iw[24], b_offset[23:22], a_mul}
  // Probe on b_offset[20]
  // Probe on b_offset[19:16]
  // Probe on b_offset[15:12]
  // Probe on b_offset[7:0]
  // Probe on b_offset[3:0]
  Multiplexer #(.Bits(4)) multiplexer_2 (.sel(RR1sel), .in_0(b_offset[3:0]), .in_1(4'b0000), .out(multiplexer_2_out));
  Multiplexer #(.Selector_Bits(2), .Bits(4)) multiplexer_3 (
    .sel(WRsel), .in_0(b_offset[15:12]), .in_1(4'b1110), .in_2(b_offset[19:16]), .in_3(4'b0000),
    .out(multiplexer_3_out));
  Multiplexer #(.Bits(32)) multiplexer_4 (
    .sel(WDsel), .in_0(multiplexer_7_out), .in_1(add_1_s), .out(multiplexer_4_out));
  // Probe on r5
  // Probe on r6
  // Probe on r7
  // Probe on r8
  // Probe on r9
  Multiplexer #(.Selector_Bits(2), .Bits(4)) multiplexer_5 (
    .sel(RR0sel), .in_0(b_offset[19:16]), .in_1(4'b1111), .in_2(b_offset[11:8]), .in_3(4'b0000),
    .out(multiplexer_5_out));
  // Probe on {iw[27:26], i_dp, iw[24], b_offset[23]}
  // Probe on a_mul
  // Probe on b_offset[20]
  // Probe on b_offset[19:16]
  // Probe on b_offset[15:12]
  // Probe on b_offset[11:8]
  // Probe on b_offset[7:4]
  // Probe on b_offset[3:0]
  RegisterFile registerfile_1 (
    .ReadReg0(multiplexer_5_out), .ReadReg1(multiplexer_2_out), .WriteData(multiplexer_4_out),
    .WriteReg(multiplexer_3_out), .WriteEn(RFW), .CLK(clk_t), .CLR(CLR), .PC(add_2_s),
    .RD0(registerfile_1_rd0), .RD1(registerfile_1_rd1), .r0(R0), .r1(r1), .r2(r2), .r3(r3), .r4(r4), .r5(r5),
    .r6(r6), .r7(r7), .r8(r8), .r9(r9), .r10(r10), .r11(r11), .r12(r12), .r13(r13), .r14(r14), .r15(r15),
    .STRreg(registerfile_1_strreg));
  // Probe on r10
  // Probe on r11
  // Probe on r12
  // Probe on r13
  // Probe on r14
  // Probe on r15
  // Probe on NCZV
  // Probe on iw[27:26]
  // Probe on i_dp
  // Probe on iw[24]
  // Probe on b_offset[23]
  // Probe on b_offset[22]
  // Probe on a_mul
  // Probe on b_offset[20]
  // Probe on b_offset[3:0]
  // Probe on b_offset[11:0]
  // Probe on {iw[27:26], i_dp}
  // Probe on iw[24]
  // Probe on {b_offset[23:22], a_mul, b_offset[20:0]}
  Multiplexer #(.Bits(32)) multiplexer_6 (
    .sel(ALUsrcB), .in_0(registerfile_1_rd1), .in_1(extender_1_extimm), .out(multiplexer_6_out));
  Comparator #(.Bits(32)) comparator_1 (
    .a({cond, iw[27:26], i_dp, iw[24], b_offset[23:22], a_mul, b_offset[20:0]}), .b(32'he2800000), .eq(DONE));  // open: gt, lt
  extender extender_1 (
    .EXT(EXTop), .IW({cond, iw[27:26], i_dp, iw[24], b_offset[23:22], a_mul, b_offset[20:0]}),
    .extimm(extender_1_extimm));
  // Probe STR_val on registerfile_1_strreg
  ALU alu_1 (
    .A(registerfile_1_rd0), .B(multiplexer_6_out),
    .iw({cond, iw[27:26], i_dp, iw[24], b_offset[23:22], a_mul, b_offset[20:0]}), .ALUOP(ALUop), .R(alu_1_r),
    .N(NCZV[0]), .Z(NCZV[1]), .C(NCZV[2]), .V(NCZV[3]));
  // Probe on extender_1_extimm
  LED led_1 (.in(DONE));
  Multiplexer #(.Bits(32)) multiplexer_7 (.sel(MR), .in_0(alu_1_r), .in_1(ramdualport_1_d), .out(multiplexer_7_out));
  // Probe Addr on alu_1_r[11:2]
  RAMDualPort #(.AddrBits(10), .Bits(32)) ramdualport_1 (
    .A(alu_1_r[11:2]), .Din(registerfile_1_strreg), .str(MW), .C(clk_t), .ld(MR), .D(ramdualport_1_d));

  // Other names for the same wires on the sheet: imm[7:0] = b_offset[7:0]; immoff[11:0] = b_offset[11:0];
  //   iw (some bits) = {cond, i_dp, b_offset[23:22], a_mul, b_offset[20:0]}; rm[3:0] = b_offset[3:0];
  //   rm_mul[3:0] = b_offset[3:0]; opmul4[3:0] = b_offset[7:4]; rs_mul[3:0] = b_offset[11:8];
  //   rd[3:0] = b_offset[15:12]; rn_mul[3:0] = b_offset[15:12]; rd_mul[3:0] = b_offset[19:16];
  //   rn[3:0] = b_offset[19:16]; l_sdt = b_offset[20]; s_dp = b_offset[20]; s_mul = b_offset[20];
  //   b_offset[21] = a_mul; opc[3:0] = {iw[24], b_offset[23:22], a_mul}; w_sdt = a_mul; b_sdt = b_offset[22];
  //   opmul6[4:0] = {iw[27:26], i_dp, iw[24], b_offset[23]}; u_sdt = b_offset[23]; l_b = iw[24]; p_sdt = iw[24];
  //   i_sdt = i_dp; opb3[2:0] = {iw[27:26], i_dp}; op2[1:0] = iw[27:26]; opmul2[1:0] = iw[27:26]; progs[3:0] = PROG

  // Notes on the sheet:
  //   CLK: Hz: 5
  //   DP
  //   MUL
  //   SDT
  //   B
endmodule

/* Test case 0_quadratic_s:
CLK CLR PROG DONE R0 
0 1 0 x x
1 1 0 x x
while (!(DONE))
C 0 0 x x
end while
0 0 0 1 3
*/

/* Test case 4_find_max_s:
CLK CLR PROG DONE R0 
0 1 4 x x
1 1 4 x x
while (!(DONE))
C 0 4 x x
end while
0 0 4 1 5
*/

/* Test case 2_max3_s:
CLK CLR PROG DONE R0 
0 1 2 x x
1 1 2 x x
while (!(DONE))
C 0 2 x x
end while
0 0 2 1 3
*/

/* Test case 1_quadratic_s:
CLK CLR PROG DONE R0
0 1 1 x x
1 1 1 x x
while (!(DONE))
C 0 1 x x
end while
0 0 1 1 18
*/

/* Test case 5_find_max_s:
CLK CLR PROG DONE R0 
0 1 5 x x
1 1 5 x x
while (!(DONE))
C 0 5 x x
end while
0 0 5 1 99
*/

/* Test case 3_max3_s:
CLK CLR PROG DONE R0 
0 1 3 x x
1 1 3 x x
while (!(DONE))
C 0 3 x x
end while
0 0 3 1 30
*/

/* Test case 6_fib_rec_s:
CLK CLR PROG DONE R0 
0 1 6 x x
1 1 6 x x
while (!(DONE))
C 0 6 x x
end while
0 0 6 1 55
*/

/* Test case 7_fib_rec_s:
CLK CLR PROG DONE R0 
0 1 7 x x
1 1 7 x x
while (!(DONE))
C 0 7 x x
end while
0 0 7 1 4181
*/
