// Digital circuit terminal.dig as structural Verilog
module terminal (
  input  [31:0] IW,
  input  clk
);

  wire comparator_1_eq, MUL_r_eq;
  wire [3:0] counter_1_out;
  wire [7:0] multiplexer_1_out;

  Counter #(.Bits(4)) counter_1 (.en(1'b1), .C(clk), .clr(1'b0), .out(counter_1_out));  // open: ovf
  // Probe on IW[27:20]
  // Probe on IW[27:24]
  // Probe on IW[27:4]
  // Probe on IW[27:22]
  // Probe on IW[7:4]
  // Probe on IW[27:21]
  Multiplexer #(.Selector_Bits(4), .Bits(8)) multiplexer_1 (
    .sel(counter_1_out), .in_0(8'h4d), .in_1(8'h4f), .in_2(8'h56), .in_3({8{1'b0}}), .in_4({8{1'b0}}),
    .in_5({8{1'b0}}), .in_6({8{1'b0}}), .in_7({8{1'b0}}), .in_8({8{1'b0}}), .in_9({8{1'b0}}),
    .in_10({8{1'b0}}), .in_11({8{1'b0}}), .in_12({8{1'b0}}), .in_13({8{1'b0}}), .in_14({8{1'b0}}),
    .in_15({8{1'b0}}), .out(multiplexer_1_out));
  Terminal terminal_1 (.D(multiplexer_1_out), .C(clk), .en(1'b1));
  Comparator #(.Bits(8)) Add_r (.a(IW[27:20]), .b(8'h8));  // open: gt, eq, lt
  Comparator #(.Bits(8)) Mov_i (.a(IW[27:20]), .b(8'h3a));  // open: gt, eq, lt
  Comparator #(.Bits(4)) b (.a(IW[27:24]), .b(4'b1010));  // open: gt, eq, lt
  Comparator #(.Bits(4)) bl (.a(IW[27:24]), .b(4'b1011));  // open: gt, eq, lt
  Comparator #(.Bits(24)) bx (.a(IW[27:4]), .b(24'h12fff1));  // open: gt, eq, lt
  Comparator #(.Bits(6)) MUL_r (.a(IW[27:22]), .b({6{1'b0}}), .eq(MUL_r_eq));  // open: gt, lt
  Comparator #(.Bits(4)) comparator_1 (.a(IW[7:4]), .b(4'b1001), .eq(comparator_1_eq));  // open: gt, lt
  Comparator #(.Bits(8)) Add__i (.a(IW[27:20]), .b(8'h28));  // open: gt, eq, lt
  Comparator #(.Bits(8)) Mov_r (.a(IW[27:20]), .b(8'h1a));  // open: gt, eq, lt
  Comparator #(.Bits(8)) Sub_i (.a(IW[27:20]), .b(8'h24));  // open: gt, eq, lt
  Comparator #(.Bits(8)) Sub_r (.a(IW[27:20]), .b(8'h4));  // open: gt, eq, lt
  Comparator #(.Bits(7)) Cmp_i (.a(IW[27:21]), .b(7'b0011010));  // open: gt, eq, lt
  Comparator #(.Bits(7)) Cmp_r (.a(IW[27:21]), .b(7'b0001010));  // open: gt, eq, lt
  Comparator #(.Bits(8)) str (.a(IW[27:20]), .b(8'h58));  // open: gt, eq, lt
  Comparator #(.Bits(8)) LDR_i (.a(IW[27:20]), .b(8'h59));  // open: gt, eq, lt
  // And and_1 has open pins: In_1=MUL_r_eq, In_2=comparator_1_eq, out=open

  // Other names for the same wires on the sheet: imm[7:0] = IW[7:0]; rm[3:0] = IW[3:0]; bits_4_7[3:0] = IW[7:4];
  //   bits_4_27[23:0] = IW[27:4]; rd[3:0] = IW[15:12]; rn[3:0] = IW[19:16]; bits_20_27[7:0] = IW[27:20];
  //   s_dp = IW[20]; bits_21_27[6:0] = IW[27:21]; opc[3:0] = IW[24:21]; bits_22_27[5:0] = IW[27:22];
  //   bits_24_27[3:0] = IW[27:24]; i_dp = IW[25]; op2[1:0] = IW[27:26]; cond[3:0] = IW[31:28]
endmodule
